// Logisim project 2_1 MUX.circ as structural Verilog: 1 circuit, main circuit main
module main (
  input  A,
  input  B,
  input  S,
  output \output 
);

  wire and_1_out, and_2_out, not_1_out, not_2_out;

  not not_1 (not_1_out, S);
  not not_2 (not_2_out, B);
  and and_1 (and_1_out, A, not_1_out);
  and and_2 (and_2_out, S, not_2_out);
  or or_1 (\output , and_1_out, and_2_out);

  // Notes on the sheet:
  //   2:1 MUX
endmodule
