// Logisim project 4_1 from 2_1.circ as structural Verilog: 2 circuits, main circuit main
module main (
  input  A,
  input  B,
  input  C,
  input  D,
  input  in_5,
  input  in_6,
  output \output 
);

  wire n2_1_mux_1_output, n2_1_mux_2_output;

  _2_1_MUX u_2_1_mux_1 (.A(A), .B(B), .S(in_5), .\output (n2_1_mux_1_output));
  _2_1_MUX u_2_1_mux_2 (.A(C), .B(D), .S(in_5), .\output (n2_1_mux_2_output));
  _2_1_MUX u_2_1_mux_3 (.A(n2_1_mux_1_output), .B(n2_1_mux_2_output), .S(in_6), .\output (\output ));

  // Notes on the sheet:
  //   S1
  //   4:1 using 2:1 MUX
  //   S0
endmodule

module _2_1_MUX (
  input  A,
  input  B,
  input  S,
  output \output 
);

  wire and_1_out, and_2_out, not_1_out, not_2_out;

  not not_1 (not_1_out, S);
  not not_2 (not_2_out, B);
  and and_1 (and_1_out, A, not_1_out);
  and and_2 (and_2_out, S, not_2_out);
  or or_1 (\output , and_1_out, and_2_out);

  // Notes on the sheet:
  //   2:1 MUX
endmodule
