// Logisim project 4bitRippleAdder.circ as structural Verilog: 2 circuits, main circuit main
module main (
  input  B3,
  input  A3,
  input  B2,
  input  A2,
  input  B1,
  input  A1,
  input  B0,
  input  A0,
  input  CIN,
  output S3,
  output S2,
  output S1,
  output S0,
  output COUT
);

  wire full_adder_1_carry, full_adder_2_carry, full_adder_3_carry;

  full_adder full_adder_1 (.A(A0), .B(B0), .C(CIN), .out_4(S0), .CARRY(full_adder_1_carry));
  full_adder full_adder_2 (.A(A1), .B(B1), .C(full_adder_1_carry), .out_4(S1), .CARRY(full_adder_2_carry));
  full_adder full_adder_3 (.A(A2), .B(B2), .C(full_adder_2_carry), .out_4(S2), .CARRY(full_adder_3_carry));
  full_adder full_adder_4 (.A(A3), .B(B3), .C(full_adder_3_carry), .out_4(S3), .CARRY(COUT));

  // Notes on the sheet:
  //   FULL ADDER
  //   4 bit ripple adder
endmodule

module full_adder (
  input  A,
  input  B,
  input  C,
  output out_4,
  output CARRY
);

  wire and_1_out, and_2_out, xor_1_out;

  xor xor_1 (xor_1_out, A, B);
  and and_1 (and_1_out, A, B);
  and and_2 (and_2_out, xor_1_out, C);
  xor xor_2 (out_4, xor_1_out, C);
  or or_1 (CARRY, and_2_out, and_1_out);

  // Notes on the sheet:
  //   SUM
endmodule
