// Logisim project 8 bit AND.circ as structural Verilog: 1 circuit, main circuit main
module main (
  input  A0,
  input  B0,
  input  A1,
  input  B1,
  input  A2,
  input  B2,
  input  A3,
  input  B3,
  input  A4,
  input  B4,
  input  A5,
  input  B5,
  input  A6,
  input  B6,
  input  A7,
  input  B7,
  output y0,
  output y1,
  output y2,
  output y3,
  output y4,
  output y5,
  output y6,
  output y7
);

  and and_1 (y0, A0, B0);
  and and_2 (y1, A1, B1);
  and and_3 (y2, A2, B2);
  and and_4 (y3, A3, B3);
  and and_5 (y4, A4, B4);
  and and_6 (y5, A5, B5);
  and and_7 (y6, A6, B6);
  and and_8 (y7, A7, B7);

  // Notes on the sheet:
  //   8 bit AND
endmodule
