// Logisim project 8 bit NOT.circ as structural Verilog: 1 circuit, main circuit main
module main (
  input  A0,
  input  A1,
  input  A2,
  input  A3,
  input  A4,
  input  A5,
  input  A6,
  input  A7,
  output y0,
  output y1,
  output y2,
  output y3,
  output y4,
  output y5,
  output y6,
  output y7
);

  not not_1 (y0, A0);
  not not_2 (y1, A1);
  not not_3 (y2, A2);
  not not_4 (y3, A3);
  not not_5 (y4, A4);
  not not_6 (y5, A5);
  not not_7 (y6, A6);
  not not_8 (y7, A7);

  // Notes on the sheet:
  //   8 bit NOT
endmodule
