// Logisim project 8 bit OR.circ as structural Verilog: 1 circuit, main circuit main
module main (
  input  A0,
  input  B0,
  input  A1,
  input  B1,
  input  A2,
  input  B2,
  input  A3,
  input  B3,
  input  A4,
  input  B4,
  input  A5,
  input  B5,
  input  A6,
  input  B6,
  input  A7,
  input  B7,
  output y0,
  output y1,
  output y2,
  output y3,
  output y4,
  output y5,
  output y6,
  output y7
);

  or or_1 (y0, A0, B0);
  or or_2 (y1, A1, B1);
  or or_3 (y2, A2, B2);
  or or_4 (y3, A3, B3);
  or or_5 (y4, A4, B4);
  or or_6 (y5, A5, B5);
  or or_7 (y6, A6, B6);
  or or_8 (y7, A7, B7);

  // Notes on the sheet:
  //   8 bit OR
endmodule
