// Logisim project ALU.circ as structural Verilog: 10 circuits, main circuit main
module main (
  input  in_1,
  input  in_2,
  input  in_3,
  input  in_4,
  input  ARITHMATIC_1,
  input  in_6,
  input  in_7,
  input  in_8,
  input  in_9,
  input  in_10,
  input  in_11,
  input  CIN,
  output out_13,
  output out_14,
  output out_15,
  output out_16,
  output out_17
);

  wire adder_1_out_10, adder_1_out_11, adder_1_out_12, adder_1_out_13, and_1_out_9, and_1_out_10,
       and_1_out_11, and_1_out_12, mux4_1_out_7, mux4_2_out_7, mux4_3_out_7, mux4_4_out_7, not_1_out_5,
       not_1_out_6, not_1_out_7, not_1_out_8, not_2_out, not_3_out, or_1_out_9, or_1_out_10, or_1_out_11,
       or_1_out_12, xor_1_out_9, xor_1_out_10, xor_1_out_11, xor_1_out_12;

  AND and_1 (
    .in_1(in_1), .in_2(in_2), .in_3(in_3), .in_4(in_4), .in_5(in_6), .in_6(in_7), .in_7(in_8), .in_8(in_9),
    .out_9(and_1_out_9), .out_10(and_1_out_10), .out_11(and_1_out_11), .out_12(and_1_out_12));
  OR or_1 (
    .in_1(in_1), .in_2(in_2), .in_3(in_3), .in_4(in_4), .in_5(in_6), .in_6(in_7), .in_7(in_8), .in_8(in_9),
    .out_9(or_1_out_9), .out_10(or_1_out_10), .out_11(or_1_out_11), .out_12(or_1_out_12));
  XOR xor_1 (
    .in_1(in_1), .in_2(in_2), .in_3(in_3), .in_4(in_4), .in_5(in_6), .in_6(in_7), .in_7(in_8), .in_8(in_9),
    .out_9(xor_1_out_9), .out_10(xor_1_out_10), .out_11(xor_1_out_11), .out_12(xor_1_out_12));
  NOT not_1 (
    .in_1(in_1), .in_2(in_2), .in_3(in_3), .in_4(in_4), .out_5(not_1_out_5), .out_6(not_1_out_6),
    .out_7(not_1_out_7), .out_8(not_1_out_8));
  ADDER adder_1 (
    .in_1(in_1), .in_2(in_2), .in_3(in_3), .in_4(in_4), .in_5(in_6), .in_6(in_7), .in_7(in_8), .in_8(in_9),
    .in_9(CIN), .out_10(adder_1_out_10), .out_11(adder_1_out_11), .out_12(adder_1_out_12),
    .out_13(adder_1_out_13), .out_14(out_17));
  not not_2 (not_2_out, in_10);
  not not_3 (not_3_out, in_11);
  MUX4 mux4_1 (
    .in_1(and_1_out_9), .in_2(or_1_out_9), .in_3(xor_1_out_9), .in_4(not_1_out_5), .in_5(in_10),
    .in_6(in_11), .out_7(mux4_1_out_7));
  MUX4 mux4_2 (
    .in_1(or_1_out_10), .in_2(and_1_out_10), .in_3(not_1_out_6), .in_4(xor_1_out_10), .in_5(in_10),
    .in_6(not_3_out), .out_7(mux4_2_out_7));
  MUX4 mux4_3 (
    .in_1(xor_1_out_11), .in_2(not_1_out_7), .in_3(and_1_out_11), .in_4(or_1_out_11), .in_5(not_2_out),
    .in_6(in_11), .out_7(mux4_3_out_7));
  MUX4 mux4_4 (
    .in_1(not_1_out_8), .in_2(xor_1_out_12), .in_3(or_1_out_12), .in_4(and_1_out_12), .in_5(not_2_out),
    .in_6(not_3_out), .out_7(mux4_4_out_7));
  MUX2 mux2_1 (.in_1(mux4_1_out_7), .in_2(adder_1_out_10), .in_3(ARITHMATIC_1), .out_4(out_13));
  MUX2 mux2_2 (.in_1(mux4_2_out_7), .in_2(adder_1_out_11), .in_3(ARITHMATIC_1), .out_4(out_14));
  MUX2 mux2_3 (.in_1(mux4_3_out_7), .in_2(adder_1_out_12), .in_3(ARITHMATIC_1), .out_4(out_15));
  MUX2 mux2_4 (.in_1(mux4_4_out_7), .in_2(adder_1_out_13), .in_3(ARITHMATIC_1), .out_4(out_16));

  // Notes on the sheet:
  //   AND
  //   OR
  //   XOR
  //   NOT
  //   SELECT AMONG LOGIC
  //   LOGIC-0
endmodule

module AND (
  input  in_1,
  input  in_2,
  input  in_3,
  input  in_4,
  input  in_5,
  input  in_6,
  input  in_7,
  input  in_8,
  output out_9,
  output out_10,
  output out_11,
  output out_12
);

  and and_1 (out_9, in_1, in_5);
  and and_2 (out_10, in_2, in_6);
  and and_3 (out_11, in_3, in_7);
  and and_4 (out_12, in_4, in_8);
endmodule

module OR (
  input  in_1,
  input  in_2,
  input  in_3,
  input  in_4,
  input  in_5,
  input  in_6,
  input  in_7,
  input  in_8,
  output out_9,
  output out_10,
  output out_11,
  output out_12
);

  or or_1 (out_9, in_1, in_5);
  or or_2 (out_10, in_2, in_6);
  or or_3 (out_11, in_3, in_7);
  or or_4 (out_12, in_4, in_8);
endmodule

module XOR (
  input  in_1,
  input  in_2,
  input  in_3,
  input  in_4,
  input  in_5,
  input  in_6,
  input  in_7,
  input  in_8,
  output out_9,
  output out_10,
  output out_11,
  output out_12
);

  xor xor_1 (out_9, in_1, in_5);
  xor xor_2 (out_10, in_2, in_6);
  xor xor_3 (out_11, in_3, in_7);
  xor xor_4 (out_12, in_4, in_8);
endmodule

module ADDER (
  input  in_1,
  input  in_2,
  input  in_3,
  input  in_4,
  input  in_5,
  input  in_6,
  input  in_7,
  input  in_8,
  input  in_9,
  output out_10,
  output out_11,
  output out_12,
  output out_13,
  output out_14
);

  wire fa_1_carry, fa_2_carry, fa_3_carry;

  FA fa_1 (.A(in_1), .B(in_5), .C(in_9), .out_4(out_10), .CARRY(fa_1_carry));
  FA fa_2 (.A(in_2), .B(in_6), .C(fa_1_carry), .out_4(out_11), .CARRY(fa_2_carry));
  FA fa_3 (.A(in_3), .B(in_7), .C(fa_2_carry), .out_4(out_12), .CARRY(fa_3_carry));
  FA fa_4 (.A(in_4), .B(in_8), .C(fa_3_carry), .out_4(out_13), .CARRY(out_14));

  // Notes on the sheet:
  //   FULL ADDER
endmodule

module FA (
  input  A,
  input  B,
  input  C,
  output out_4,
  output CARRY
);

  wire and_1_out, and_2_out, xor_1_out;

  xor xor_1 (xor_1_out, A, B);
  and and_1 (and_1_out, A, B);
  and and_2 (and_2_out, xor_1_out, C);
  xor xor_2 (out_4, xor_1_out, C);
  or or_1 (CARRY, and_2_out, and_1_out);

  // Notes on the sheet:
  //   SUM
endmodule

module NOT (
  input  in_1,
  input  in_2,
  input  in_3,
  input  in_4,
  output out_5,
  output out_6,
  output out_7,
  output out_8
);

  not not_1 (out_5, in_1);
  not not_2 (out_6, in_2);
  not not_3 (out_7, in_3);
  not not_4 (out_8, in_4);
endmodule

module MUX4 (
  input  in_1,
  input  in_2,
  input  in_3,
  input  in_4,
  input  in_5,
  input  in_6,
  output out_7
);

  wire and_1_out, and_2_out, and_3_out, and_4_out, not_1_out, not_2_out;

  not not_1 (not_1_out, in_5);
  not not_2 (not_2_out, in_6);
  and and_1 (and_1_out, in_1, not_1_out, not_2_out);
  and and_2 (and_2_out, in_2, not_1_out, in_6);
  and and_3 (and_3_out, in_3, in_5, not_2_out);
  and and_4 (and_4_out, in_4, in_5, in_6);
  or or_1 (out_7, and_1_out, and_2_out, and_3_out, and_4_out);
endmodule

module MUX2 (
  input  in_1,
  input  in_2,
  input  in_3,
  output out_4
);

  wire and_1_out, and_2_out, not_1_out;

  not not_1 (not_1_out, in_3);
  and and_1 (and_1_out, in_1, not_1_out);
  and and_2 (and_2_out, in_2, in_3);
  or or_1 (out_4, and_1_out, and_2_out);
endmodule

module PRAC (
  input  in_1,
  input  in_2,
  input  in_3,
  input  in_4,
  input  ARITHMATIC_1,
  input  in_6,
  input  in_7,
  input  in_8,
  input  in_9,
  input  in_10,
  input  in_11,
  input  CIN,
  output out_13,
  output out_14,
  output out_15,
  output out_16,
  output out_17
);

  wire adder_1_out_10, adder_1_out_11, adder_1_out_12, adder_1_out_13, and_1_out_9, and_1_out_10,
       and_1_out_11, and_1_out_12, mux4_1_out_7, mux4_2_out_7, mux4_3_out_7, mux4_4_out_7, not_1_out_5,
       not_1_out_6, not_1_out_7, not_1_out_8, not_2_out, not_3_out, or_1_out_9, or_1_out_10, or_1_out_11,
       or_1_out_12, xor_1_out_9, xor_1_out_10, xor_1_out_11, xor_1_out_12;

  AND and_1 (
    .in_1(in_1), .in_2(in_2), .in_3(in_3), .in_4(in_4), .in_5(in_6), .in_6(in_7), .in_7(in_8), .in_8(in_9),
    .out_9(and_1_out_9), .out_10(and_1_out_10), .out_11(and_1_out_11), .out_12(and_1_out_12));
  OR or_1 (
    .in_1(in_1), .in_2(in_2), .in_3(in_3), .in_4(in_4), .in_5(in_6), .in_6(in_7), .in_7(in_8), .in_8(in_9),
    .out_9(or_1_out_9), .out_10(or_1_out_10), .out_11(or_1_out_11), .out_12(or_1_out_12));
  XOR xor_1 (
    .in_1(in_1), .in_2(in_2), .in_3(in_3), .in_4(in_4), .in_5(in_6), .in_6(in_7), .in_7(in_8), .in_8(in_9),
    .out_9(xor_1_out_9), .out_10(xor_1_out_10), .out_11(xor_1_out_11), .out_12(xor_1_out_12));
  NOT not_1 (
    .in_1(in_1), .in_2(in_2), .in_3(in_3), .in_4(in_4), .out_5(not_1_out_5), .out_6(not_1_out_6),
    .out_7(not_1_out_7), .out_8(not_1_out_8));
  ADDER adder_1 (
    .in_1(in_1), .in_2(in_2), .in_3(in_3), .in_4(in_4), .in_5(in_6), .in_6(in_7), .in_7(in_8), .in_8(in_9),
    .in_9(CIN), .out_10(adder_1_out_10), .out_11(adder_1_out_11), .out_12(adder_1_out_12),
    .out_13(adder_1_out_13), .out_14(out_17));
  not not_2 (not_2_out, in_10);
  not not_3 (not_3_out, in_11);
  MUX4 mux4_1 (
    .in_1(and_1_out_9), .in_2(or_1_out_9), .in_3(xor_1_out_9), .in_4(not_1_out_5), .in_5(in_10),
    .in_6(in_11), .out_7(mux4_1_out_7));
  MUX4 mux4_2 (
    .in_1(or_1_out_10), .in_2(and_1_out_10), .in_3(not_1_out_6), .in_4(xor_1_out_10), .in_5(in_10),
    .in_6(not_3_out), .out_7(mux4_2_out_7));
  MUX4 mux4_3 (
    .in_1(xor_1_out_11), .in_2(not_1_out_7), .in_3(and_1_out_11), .in_4(or_1_out_11), .in_5(not_2_out),
    .in_6(in_11), .out_7(mux4_3_out_7));
  MUX4 mux4_4 (
    .in_1(not_1_out_8), .in_2(xor_1_out_12), .in_3(or_1_out_12), .in_4(and_1_out_12), .in_5(not_2_out),
    .in_6(not_3_out), .out_7(mux4_4_out_7));
  MUX2 mux2_1 (.in_1(mux4_1_out_7), .in_2(adder_1_out_10), .in_3(ARITHMATIC_1), .out_4(out_13));
  MUX2 mux2_2 (.in_1(mux4_2_out_7), .in_2(adder_1_out_11), .in_3(ARITHMATIC_1), .out_4(out_14));
  MUX2 mux2_3 (.in_1(mux4_3_out_7), .in_2(adder_1_out_12), .in_3(ARITHMATIC_1), .out_4(out_15));
  MUX2 mux2_4 (.in_1(mux4_4_out_7), .in_2(adder_1_out_13), .in_3(ARITHMATIC_1), .out_4(out_16));

  // Notes on the sheet:
  //   AND
  //   OR
  //   XOR
  //   NOT
  //   SELECT AMONG LOGIC
  //   LOGIC-0
endmodule
