// Logisim project B.circ as structural Verilog
module PRAC (
  input  A1,
  input  A2,
  input  A3,
  input  A4,
  input  in_5,
  input  in_6,
  output Y4,
  output Y3,
  output Y2,
  output Y1
);

  wire decoder_1_out_3, decoder_1_out_4, decoder_1_out_5, decoder_1_out_6;

  DECODER decoder_1 (
    .in_1(in_5), .in_2(in_6), .out_3(decoder_1_out_3), .out_4(decoder_1_out_4), .out_5(decoder_1_out_5),
    .out_6(decoder_1_out_6));
  assign Y4 = decoder_1_out_6 ? A1 : 1'bz;  // Controlled_Buffer controlled_buffer_1
  assign Y3 = decoder_1_out_5 ? A1 : 1'bz;  // Controlled_Buffer controlled_buffer_2
  assign Y2 = decoder_1_out_4 ? A1 : 1'bz;  // Controlled_Buffer controlled_buffer_3
  assign Y1 = decoder_1_out_3 ? A1 : 1'bz;  // Controlled_Buffer controlled_buffer_4
  assign Y4 = decoder_1_out_5 ? A2 : 1'bz;  // Controlled_Buffer controlled_buffer_5
  assign Y3 = decoder_1_out_4 ? A2 : 1'bz;  // Controlled_Buffer controlled_buffer_6
  assign Y2 = decoder_1_out_3 ? A2 : 1'bz;  // Controlled_Buffer controlled_buffer_7
  assign Y1 = decoder_1_out_6 ? A2 : 1'bz;  // Controlled_Buffer controlled_buffer_8
  assign Y4 = decoder_1_out_4 ? A3 : 1'bz;  // Controlled_Buffer controlled_buffer_9
  assign Y3 = decoder_1_out_3 ? A3 : 1'bz;  // Controlled_Buffer controlled_buffer_10
  assign Y2 = decoder_1_out_6 ? A3 : 1'bz;  // Controlled_Buffer controlled_buffer_11
  assign Y1 = decoder_1_out_5 ? A3 : 1'bz;  // Controlled_Buffer controlled_buffer_12
  assign Y4 = decoder_1_out_3 ? A4 : 1'bz;  // Controlled_Buffer controlled_buffer_13
  assign Y3 = decoder_1_out_6 ? A4 : 1'bz;  // Controlled_Buffer controlled_buffer_14
  assign Y2 = decoder_1_out_5 ? A4 : 1'bz;  // Controlled_Buffer controlled_buffer_15
  assign Y1 = decoder_1_out_4 ? A4 : 1'bz;  // Controlled_Buffer controlled_buffer_16
endmodule

module DECODER (
  input  in_1,
  input  in_2,
  output out_3,
  output out_4,
  output out_5,
  output out_6
);

  wire not_1_out, not_2_out;

  not not_1 (not_1_out, in_1);
  not not_2 (not_2_out, in_2);
  and and_1 (out_3, not_1_out, not_2_out);
  and and_2 (out_4, not_1_out, in_2);
  and and_3 (out_5, in_1, not_2_out);
  and and_4 (out_6, in_1, in_2);
endmodule
