// Logisim project Register_file.circ as structural Verilog
module Register_File (
  input  Clear,
  input  [3:0] Write_Port,
  input  [1:0] Write_set,
  input  [1:0] Read_set,
  input  Clock,
  output [3:0] Read_Port
);

  wire and_1_out, and_2_out, and_3_out, and_4_out, decoder_1_out0, decoder_1_out1, decoder_1_out2,
       decoder_1_out3;
  wire [3:0] register_1_q, register_2_q, register_3_q, register_4_q;

  Decoder #(.select(2)) decoder_1 (
    .out0(decoder_1_out0), .out1(decoder_1_out1), .out2(decoder_1_out2), .out3(decoder_1_out3),
    .sel(Write_set));  // open: en
  and and_1 (and_1_out, decoder_1_out0, Clear);
  and and_2 (and_2_out, decoder_1_out1, Clear);
  and and_3 (and_3_out, decoder_1_out2, Clear);
  and and_4 (and_4_out, decoder_1_out3, Clear);
  Register #(.width(4)) register_1 (.D(Write_Port), .en(and_1_out), .Q(register_1_q), .clk(Clock), .clr(1'b0));
  Register #(.width(4)) register_2 (.D(Write_Port), .en(and_2_out), .Q(register_2_q), .clk(Clock), .clr(1'b0));
  Register #(.width(4)) register_3 (.D(Write_Port), .en(and_3_out), .Q(register_3_q), .clk(Clock), .clr(1'b0));
  Register #(.width(4)) register_4 (.D(Write_Port), .en(and_4_out), .Q(register_4_q), .clk(Clock), .clr(1'b0));
  Multiplexer #(.select(2), .width(4)) multiplexer_1 (
    .in0(register_1_q), .in1(register_2_q), .in2(register_3_q), .in3(register_4_q), .out(Read_Port),
    .sel(Read_set));  // open: en
endmodule
