// Logisim project carryLookAhead.circ as structural Verilog: 3 circuits, main circuit main
module main (
  input  B7,
  input  A7,
  input  B6,
  input  A6,
  input  B5,
  input  A5,
  input  B4,
  input  A4,
  input  B3,
  input  A3,
  input  B2,
  input  A2,
  input  B1,
  input  A1,
  input  B0,
  input  A0,
  input  CIN,
  output COUT,
  output S7,
  output S6,
  output S5,
  output S4,
  output S3,
  output S2,
  output S1,
  output S0
);

  wire n4_bit_adder_2_cout;

  _4_BIT_ADDER u_4_bit_adder_1 (
    .B3(B7), .A3(A7), .B2(B6), .A2(A6), .B1(B5), .A1(A5), .B0(B4), .A0(A4), .CIN(n4_bit_adder_2_cout),
    .COUT(COUT), .S3(S7), .S2(S6), .S1(S5), .S0(S4));
  _4_BIT_ADDER u_4_bit_adder_2 (
    .B3(B3), .A3(A3), .B2(B2), .A2(A2), .B1(B1), .A1(A1), .B0(B0), .A0(A0), .CIN(CIN),
    .COUT(n4_bit_adder_2_cout), .S3(S3), .S2(S2), .S1(S1), .S0(S0));
endmodule

module _4_BIT_ADDER (
  input  B3,
  input  A3,
  input  B2,
  input  A2,
  input  B1,
  input  A1,
  input  B0,
  input  A0,
  input  CIN,
  output COUT,
  output S3,
  output S2,
  output S1,
  output S0
);

  wire and_1_out, and_2_out, and_3_out, and_4_out, n4_bit_cla_1_c1, n4_bit_cla_1_c2, n4_bit_cla_1_c3,
       xor_1_out, xor_2_out, xor_3_out, xor_4_out;

  xor xor_1 (xor_1_out, B3, A3);
  and and_1 (and_1_out, B3, A3);
  xor xor_2 (xor_2_out, B2, A2);
  and and_2 (and_2_out, B2, A2);
  xor xor_3 (xor_3_out, B1, A1);
  and and_3 (and_3_out, B1, A1);
  xor xor_4 (xor_4_out, B0, A0);
  and and_4 (and_4_out, B0, A0);
  _4_BIT_CLA u_4_bit_cla_1 (
    .P3(xor_1_out), .G3(and_1_out), .P2(xor_2_out), .G2(and_2_out), .P1(xor_3_out), .G1(and_3_out),
    .P0(xor_4_out), .G0(and_4_out), .C0(CIN), .C4(COUT), .C3(n4_bit_cla_1_c3), .C2(n4_bit_cla_1_c2),
    .C1(n4_bit_cla_1_c1));
  xor xor_5 (S0, CIN, xor_4_out);
  xor xor_6 (S3, xor_1_out, n4_bit_cla_1_c3);
  xor xor_7 (S2, xor_2_out, n4_bit_cla_1_c2);
  xor xor_8 (S1, xor_3_out, n4_bit_cla_1_c1);
endmodule

module _4_BIT_CLA (
  input  P3,
  input  G3,
  input  P2,
  input  G2,
  input  P1,
  input  G1,
  input  P0,
  input  G0,
  input  C0,
  output C4,
  output C3,
  output C2,
  output C1
);

  wire and_1_out, and_2_out, and_3_out, and_4_out, and_5_out, and_6_out, and_7_out, and_8_out, and_9_out,
       and_10_out;

  and and_1 (and_1_out, P3, P2, P1, P0, C0);
  and and_2 (and_2_out, P3, P2, P1, G0);
  and and_3 (and_3_out, P3, P2, G1);
  and and_4 (and_4_out, P3, G2);
  and and_5 (and_5_out, P2, G1, P0, C0);
  and and_6 (and_6_out, P2, P1, G0);
  and and_7 (and_7_out, G1, P2);
  and and_8 (and_8_out, P1, P0, C0);
  and and_9 (and_9_out, P1, G0);
  and and_10 (and_10_out, P0, C0);
  or or_1 (C4, and_1_out, and_2_out, and_3_out, and_4_out, G3);
  or or_2 (C3, and_5_out, and_6_out, and_7_out, G2);
  or or_3 (C2, and_8_out, and_9_out, G1);
  or or_4 (C1, and_10_out, G0);
endmodule
