// Logisim project circuit.circ as structural Verilog: 2 circuits, main circuit main
module main (
  input  in_1,
  input  in_2,
  input  in_3,
  input  in_4,
  output \output 
);

  wire and_1_out, not_1_out, or_1_out, xor_1_out;

  and and_1 (and_1_out, in_1, in_2);
  or or_1 (or_1_out, in_1, in_2);
  not not_1 (not_1_out, in_1);
  xor xor_1 (xor_1_out, in_1, in_2);
  _4_1_MUX u_4_1_mux_1 (
    .in_1(and_1_out), .in_2(or_1_out), .in_3(not_1_out), .in_4(xor_1_out), .in_5(in_3), .in_6(in_4),
    .out_7(\output ));

  // Notes on the sheet:
  //   A
  //   B
  //   S1
  //   S0
endmodule

module _4_1_MUX (
  input  in_1,
  input  in_2,
  input  in_3,
  input  in_4,
  input  in_5,
  input  in_6,
  output out_7
);

  wire and_1_out, and_2_out, and_3_out, and_4_out, not_1_out, not_2_out;

  not not_1 (not_1_out, in_5);
  not not_2 (not_2_out, in_6);
  and and_1 (and_1_out, in_1, not_1_out, not_2_out);
  and and_2 (and_2_out, in_2, not_1_out, not_1_out, in_6);
  and and_3 (and_3_out, in_3, in_5, not_2_out);
  and and_4 (and_4_out, in_4, not_1_out, not_2_out);
  or or_1 (out_7, and_1_out, and_2_out, and_3_out, and_4_out);
endmodule
