// Logisim project fullAdder.circ as structural Verilog: 1 circuit, main circuit main
module main (
  input  A,
  input  B,
  input  C,
  output out_4,
  output CARRY
);

  wire and_1_out, and_2_out, xor_1_out;

  xor xor_1 (xor_1_out, A, B);
  and and_1 (and_1_out, A, B);
  and and_2 (and_2_out, xor_1_out, C);
  xor xor_2 (out_4, xor_1_out, C);
  or or_1 (CARRY, and_2_out, and_1_out);

  // Notes on the sheet:
  //   SUM
endmodule
